# Fritzing sketch HC-SR04_Test (saved by Fritzing 0.9.2b)
breadboards: 1

parts:
  Composant1 = SRF05 Ultrasonic Rangefinder
  Composant2 = Arduino Uno (Rev3)

nets:
  VCC: Composant1.VCC, Composant2.5V
  N1: Composant1.Trig, Composant2.D13/SCK
  N2: Composant1.Echo, Composant2.D12/MISO
  GND: Composant1.GND, Composant2.GND
