# Fritzing sketch HC-SR04_with_LCD (saved by Fritzing 0.9.2b)
breadboards: 1

parts:
  Composant1 = SRF05 Ultrasonic Rangefinder
  Composant2 = Arduino Uno (Rev3)
  LCD1 = LCD screen

nets:
  VCC: Composant1.VCC, Composant2.5V, LCD1.VDD, LCD1.LED+
  N1: Composant1.Trig, Composant2.D13/SCK
  N2: Composant1.Echo, Composant2.D12/MISO
  GND: Composant1.GND, Composant2.GND, LCD1.VSS, LCD1.V0, LCD1.LED-
  N3: Composant2.D9_PWM, LCD1.E
  N4: Composant2.D10_PWM/SS, LCD1.R/W
  N5: Composant2.D11_PWM/MOSI, LCD1.RS
  N6: Composant2.D2, LCD1.DB4
  N7: Composant2.D3_PWM, LCD1.DB5
  N8: Composant2.D4, LCD1.DB6
  N9: Composant2.D5_PWM, LCD1.DB7
